// Logisim project ALU PROJECT.circ as structural Verilog
module full_adder (
  input  A,
  input  B,
  input  C_in,
  output sum,
  output C_out
);

  wire and_1_out, and_2_out, xor_1_out;

  xor xor_1 (xor_1_out, A, B);
  and and_1 (and_1_out, A, B);
  and and_2 (and_2_out, xor_1_out, C_in);
  xor xor_2 (sum, xor_1_out, C_in);
  or or_1 (C_out, and_1_out, and_2_out);
endmodule

module _4_bit_Adder (
  input  in_1,
  input  in_2,
  input  in_3,
  input  in_4,
  input  in_5,
  input  in_6,
  input  in_7,
  input  in_8,
  input  in_9,
  output out_10,
  output out_11,
  output out_12,
  output out_13,
  output out_14
);

  wire full_adder_2_c_out, full_adder_3_c_out, full_adder_4_c_out;

  full_adder full_adder_1 (.A(in_1), .B(in_5), .C_in(full_adder_2_c_out), .sum(out_11), .C_out(out_10));
  full_adder full_adder_2 (.A(in_2), .B(in_6), .C_in(full_adder_3_c_out), .sum(out_12), .C_out(full_adder_2_c_out));
  full_adder full_adder_3 (.A(in_3), .B(in_7), .C_in(full_adder_4_c_out), .sum(out_13), .C_out(full_adder_3_c_out));
  full_adder full_adder_4 (.A(in_4), .B(in_8), .C_in(in_9), .sum(out_14), .C_out(full_adder_4_c_out));
endmodule

module Arithmatic_Unit (
  input  in_1,
  input  in_2,
  input  in_3,
  input  in_4,
  input  in_5,
  input  in_6,
  input  in_7,
  input  in_8,
  input  in_9,
  input  in_10,
  input  in_11,
  input  in_12,
  input  in_13,
  input  in_14,
  input  in_15,
  input  in_16,
  input  in_17,
  input  in_18,
  input  in_19,
  input  in_20,
  input  in_21,
  input  in_22,
  input  in_23,
  output out_24,
  output out_25,
  output out_26,
  output out_27,
  output out_28,
  output out_29,
  output out_30
);

  wire n4_bit_adder_1_out_11, n4_bit_adder_1_out_12, n4_bit_adder_1_out_13, n4_bit_adder_1_out_14,
       n5_bit_storage_1_y0, n5_bit_storage_1_y1, n5_bit_storage_1_y2, n5_bit_storage_1_y3, not_1_out,
       or_1_out, or_2_out, trans_1_out_6, trans_1_out_7, trans_1_out_8, trans_1_out_9, trans_2_out_6,
       trans_2_out_7, trans_2_out_8, trans_2_out_9, xor_ic_1_out_9, xor_ic_1_out_10, xor_ic_1_out_11,
       xor_ic_1_out_12, xor_ic_2_out_9, xor_ic_2_out_10, xor_ic_2_out_11, xor_ic_2_out_12, xor_ic_3_out_9,
       xor_ic_3_out_10, xor_ic_3_out_11, xor_ic_3_out_12;

  trans trans_1 (
    .in_1(in_4), .in_2(in_6), .in_3(in_9), .in_4(in_11), .in_5(in_13), .out_6(trans_1_out_6),
    .out_7(trans_1_out_7), .out_8(trans_1_out_8), .out_9(trans_1_out_9));
  trans trans_2 (
    .in_1(in_15), .in_2(in_16), .in_3(in_19), .in_4(in_21), .in_5(in_22), .out_6(trans_2_out_6),
    .out_7(trans_2_out_7), .out_8(trans_2_out_8), .out_9(trans_2_out_9));
  trans trans_3 (
    .in_1(n5_bit_storage_1_y0), .in_2(n5_bit_storage_1_y1), .in_3(n5_bit_storage_1_y2),
    .in_4(n5_bit_storage_1_y3), .in_5(in_1), .out_6(trans_1_out_6), .out_7(trans_1_out_7),
    .out_8(trans_1_out_8), .out_9(trans_1_out_9));
  trans trans_4 (
    .in_5(in_14), .out_6(trans_2_out_6), .out_7(trans_2_out_7), .out_8(trans_2_out_8), .out_9(trans_2_out_9));  // open: in_1, in_2, in_3, in_4
  _4_bit_Adder u_4_bit_adder_1 (
    .in_1(xor_ic_1_out_9), .in_2(xor_ic_1_out_10), .in_3(xor_ic_1_out_11), .in_4(xor_ic_1_out_12),
    .in_5(xor_ic_2_out_9), .in_6(xor_ic_2_out_10), .in_7(xor_ic_2_out_11), .in_8(xor_ic_2_out_12),
    .in_9(in_18), .out_10(out_25), .out_11(n4_bit_adder_1_out_11), .out_12(n4_bit_adder_1_out_12),
    .out_13(n4_bit_adder_1_out_13), .out_14(n4_bit_adder_1_out_14));
  Xor_IC xor_ic_1 (
    .in_1(trans_1_out_6), .in_2(in_2), .in_3(trans_1_out_7), .in_4(in_2), .in_5(trans_1_out_8), .in_6(in_2),
    .in_7(trans_1_out_9), .in_8(in_2), .out_9(xor_ic_1_out_9), .out_10(xor_ic_1_out_10),
    .out_11(xor_ic_1_out_11), .out_12(xor_ic_1_out_12));
  Xor_IC xor_ic_2 (
    .in_1(trans_2_out_6), .in_2(in_23), .in_3(trans_2_out_7), .in_4(in_23), .in_5(trans_2_out_8),
    .in_6(in_23), .in_7(trans_2_out_9), .in_8(in_23), .out_9(xor_ic_2_out_9), .out_10(xor_ic_2_out_10),
    .out_11(xor_ic_2_out_11), .out_12(xor_ic_2_out_12));
  not not_1 (not_1_out, out_25);
  _4_bit_Adder u_4_bit_adder_2 (
    .in_1(xor_ic_3_out_9), .in_2(xor_ic_3_out_10), .in_3(xor_ic_3_out_11), .in_4(xor_ic_3_out_12),
    .in_5(in_17), .in_6(in_17), .in_7(in_17), .in_8(in_17), .in_9(or_2_out), .out_10(out_26),
    .out_11(out_27), .out_12(out_28), .out_13(out_29), .out_14(out_30));
  and and_1 (out_24, in_3, not_1_out);
  Xor_IC xor_ic_3 (
    .in_1(n4_bit_adder_1_out_11), .in_2(or_1_out), .in_3(n4_bit_adder_1_out_12), .in_4(or_1_out),
    .in_5(n4_bit_adder_1_out_13), .in_6(or_1_out), .in_7(n4_bit_adder_1_out_14), .in_8(or_1_out),
    .out_9(xor_ic_3_out_9), .out_10(xor_ic_3_out_10), .out_11(xor_ic_3_out_11), .out_12(xor_ic_3_out_12));
  or or_1 (or_1_out, in_8, out_24);
  or or_2 (or_2_out, in_20, out_24);
  _5_Bit_STORAGE u_5_bit_storage_1 (
    .Clk(in_5), .PRESET(in_7), .EN(in_10), .RESET(in_12), .Y3(n5_bit_storage_1_y3), .Y2(n5_bit_storage_1_y2),
    .Y1(n5_bit_storage_1_y1), .Y0(n5_bit_storage_1_y0));  // open: A4, A0, A1, A2, A3, Y4
  Hex_Digit_Display hex_digit_display_1 (.value({out_27, out_28, out_29, out_30}));  // open: dp
endmodule

module Xor_IC (
  input  in_1,
  input  in_2,
  input  in_3,
  input  in_4,
  input  in_5,
  input  in_6,
  input  in_7,
  input  in_8,
  output out_9,
  output out_10,
  output out_11,
  output out_12
);

  xor A (out_9, in_1, in_2);
  xor A_2 (out_10, in_3, in_4);
  xor A_3 (out_11, in_5, in_6);
  xor A_4 (out_12, in_7, in_8);
endmodule

module trans (
  input  in_1,
  input  in_2,
  input  in_3,
  input  in_4,
  input  in_5,
  output out_6,
  output out_7,
  output out_8,
  output out_9
);

  wire not_1_out, not_2_out, not_3_out, not_4_out;

  not not_1 (not_1_out, in_5);
  // Transmission_Gate transmission_1: pin names not known; wires that end beside it: in_1, not_1_out, in_5, out_6
  not not_2 (not_2_out, in_5);
  // Transmission_Gate transmission_2: pin names not known; wires that end beside it: in_2, not_2_out, in_5, out_7
  not not_3 (not_3_out, in_5);
  // Transmission_Gate transmission_3: pin names not known; wires that end beside it: in_3, not_3_out, in_5, out_8
  not not_4 (not_4_out, in_5);
  // Transmission_Gate transmission_4: pin names not known; wires that end beside it: in_4, not_4_out, in_5, out_9
endmodule

module _5_Bit_STORAGE (
  input  Clk,
  input  PRESET,
  input  EN,
  input  RESET,
  input  A4,
  input  A0,
  input  A1,
  input  A2,
  input  A3,
  output Y2,
  output Y4,
  output Y3,
  output Y1,
  output Y0
);

  D_Flip_Flop d_ff_1 (.clk(Clk), .D(A0), .Q(Y4), .preset(PRESET), .en(EN), .reset(RESET));  // open: Qn
  D_Flip_Flop d_ff_2 (.clk(Clk), .D(A1), .Q(Y3), .preset(PRESET), .en(EN), .reset(RESET));  // open: Qn
  D_Flip_Flop d_ff_3 (.clk(Clk), .D(A2), .Q(Y2), .preset(PRESET), .en(EN), .reset(RESET));  // open: Qn
  D_Flip_Flop d_ff_4 (.clk(Clk), .D(A3), .Q(Y1), .preset(PRESET), .en(EN), .reset(RESET));  // open: Qn
  D_Flip_Flop d_ff_5 (.clk(Clk), .D(A4), .Q(Y0), .preset(PRESET), .en(EN), .reset(RESET));  // open: Qn
endmodule

module Logic_Unit (
  input  Y13,
  input  B3,
  input  B2,
  input  B1,
  input  B0,
  input  A3,
  input  A2,
  input  A1,
  input  A0,
  input  Y10,
  input  Y14,
  input  Y11,
  input  Y15,
  input  Y12,
  output L0,
  output L1,
  output L2,
  output L3
);

  wire and_1_out, and_2_out, and_3_out, and_4_out, nand_1_out, nand_2_out, nand_3_out, nand_4_out, nor_1_out,
       nor_2_out, nor_3_out, nor_4_out, or_1_out, or_2_out, or_3_out, or_4_out, xnor_1_out, xnor_2_out,
       xnor_3_out, xnor_4_out, xor_1_out, xor_2_out, xor_3_out, xor_4_out;

  trans trans_1 (
    .in_1(nor_4_out), .in_2(nor_3_out), .in_3(nor_2_out), .in_4(nor_1_out), .in_5(Y13), .out_6(L3),
    .out_7(L2), .out_8(L1), .out_9(L0));
  trans trans_2 (
    .in_1(xor_4_out), .in_2(xor_3_out), .in_3(xor_2_out), .in_4(xor_1_out), .in_5(Y14), .out_6(L3),
    .out_7(L2), .out_8(L1), .out_9(L0));
  trans trans_3 (
    .in_1(xnor_4_out), .in_2(xnor_3_out), .in_3(xnor_2_out), .in_4(xnor_1_out), .in_5(Y15), .out_6(L3),
    .out_7(L2), .out_8(L1), .out_9(L0));
  nor nor_1 (nor_1_out, B3, A3);
  nor nor_2 (nor_2_out, B2, A2);
  nor nor_3 (nor_3_out, B1, A1);
  nor nor_4 (nor_4_out, B0, A0);
  xor xor_1 (xor_1_out, B3, A3);
  xor xor_2 (xor_2_out, B2, A2);
  xor xor_3 (xor_3_out, B1, A1);
  xor xor_4 (xor_4_out, B0, A0);
  xnor xnor_1 (xnor_1_out, B3, A3);
  xnor xnor_2 (xnor_2_out, B2, A2);
  xnor xnor_3 (xnor_3_out, B1, A1);
  xnor xnor_4 (xnor_4_out, B0, A0);
  and and_1 (and_1_out, B3, A3);
  and and_2 (and_2_out, B2, A2);
  and and_3 (and_3_out, B1, A1);
  and and_4 (and_4_out, B0, A0);
  or or_1 (or_1_out, B3, A3);
  or or_2 (or_2_out, B2, A2);
  or or_3 (or_3_out, B1, A1);
  or or_4 (or_4_out, B0, A0);
  nand nand_1 (nand_1_out, B3, A3);
  nand nand_2 (nand_2_out, B2, A2);
  nand nand_3 (nand_3_out, B1, A1);
  nand nand_4 (nand_4_out, B0, A0);
  trans trans_4 (
    .in_1(and_1_out), .in_2(and_2_out), .in_3(and_3_out), .in_4(and_4_out), .in_5(Y10), .out_6(L0),
    .out_7(L1), .out_8(L2), .out_9(L3));
  trans trans_5 (
    .in_1(or_1_out), .in_2(or_2_out), .in_3(or_3_out), .in_4(or_4_out), .in_5(Y11), .out_6(L0), .out_7(L1),
    .out_8(L2), .out_9(L3));
  trans trans_6 (
    .in_1(nand_1_out), .in_2(nand_2_out), .in_3(nand_3_out), .in_4(nand_4_out), .in_5(Y12), .out_6(L0),
    .out_7(L1), .out_8(L2), .out_9(L3));
endmodule

module ALU_Assembly (
  input  in_1,
  input  in_2,
  input  in_3,
  input  in_4,
  input  A0,
  input  in_6,
  input  in_7,
  input  in_8,
  input  in_9,
  input  in_10,
  input  in_11,
  input  in_12,
  input  in_13,
  input  in_14,
  input  B0,
  input  in_16,
  input  Arithmatic_EN,
  input  in_18,
  input  in_19,
  input  in_20,
  input  S0,
  output NEG,
  output C_O1,
  output out_24,
  output out_25,
  output out_26,
  output Y0,
  output out_28,
  output out_29,
  output out_30,
  output Y0_2,
  output out_32,
  output out_33,
  output out_34,
  output out_35
);

  wire demultiplexer_1_out0, demultiplexer_1_out1, demultiplexer_1_out2, demultiplexer_1_out3,
       demultiplexer_1_out4, demultiplexer_1_out5, demultiplexer_1_out6, demultiplexer_1_out7,
       demultiplexer_1_out8, demultiplexer_1_out9, demultiplexer_1_out10, demultiplexer_1_out11,
       demultiplexer_1_out12, demultiplexer_1_out13, demultiplexer_1_out14, demultiplexer_1_out15, not_1_out,
       or_1_out, or_2_out, or_3_out, trans_1_out_7, trans_1_out_8, trans_1_out_9, trans_2_out_6,
       trans_2_out_7, trans_2_out_8, trans_2_out_9;

  Demultiplexer #(.select(4), .enable("false")) demultiplexer_1 (
    .out0(demultiplexer_1_out0), .out1(demultiplexer_1_out1), .out2(demultiplexer_1_out2),
    .out3(demultiplexer_1_out3), .out4(demultiplexer_1_out4), .out5(demultiplexer_1_out5),
    .out6(demultiplexer_1_out6), .out7(demultiplexer_1_out7), .out8(demultiplexer_1_out8),
    .out9(demultiplexer_1_out9), .out10(demultiplexer_1_out10), .out11(demultiplexer_1_out11),
    .out12(demultiplexer_1_out12), .out13(demultiplexer_1_out13), .out14(demultiplexer_1_out14),
    .out15(demultiplexer_1_out15), .in(in_16), .sel({in_18, in_19, in_20, S0}));
  Logic_Unit logic_unit_1 (
    .L0(out_32), .L1(out_33), .L2(out_34), .L3(out_35), .Y13(demultiplexer_1_out13),
    .Y15(demultiplexer_1_out14), .Y14(demultiplexer_1_out15), .B3(in_12), .B2(in_13), .B1(in_14), .B0(B0),
    .A3(in_2), .A2(in_3), .A1(in_4), .A0(A0), .Y10(demultiplexer_1_out10), .Y11(demultiplexer_1_out11),
    .Y12(demultiplexer_1_out12));
  trans trans_1 (
    .in_1(demultiplexer_1_out0), .in_2(demultiplexer_1_out1), .in_3(demultiplexer_1_out2),
    .in_4(demultiplexer_1_out3), .in_5(Arithmatic_EN), .out_7(trans_1_out_7), .out_8(trans_1_out_8),
    .out_9(trans_1_out_9));  // open: out_6
  trans trans_2 (
    .in_1(demultiplexer_1_out4), .in_2(demultiplexer_1_out5), .in_3(demultiplexer_1_out6),
    .in_4(demultiplexer_1_out7), .in_5(Arithmatic_EN), .out_6(trans_2_out_6), .out_7(trans_2_out_7),
    .out_8(trans_2_out_8), .out_9(trans_2_out_9));
  not not_1 (not_1_out, trans_2_out_8);
  Arithmatic_Unit arithmatic_unit_1 (
    .in_1(in_6), .in_3(trans_1_out_7), .in_5(in_7), .in_4(in_2), .in_7(in_8), .in_6(in_3), .in_8(in_1),
    .in_10(trans_2_out_9), .in_9(in_4), .in_12(in_9), .in_11(A0), .in_13(in_10), .in_14(trans_2_out_8),
    .in_15(in_12), .in_16(in_13), .in_17(trans_1_out_9), .in_19(in_14), .in_20(or_2_out), .in_21(B0),
    .in_22(not_1_out), .out_24(NEG), .out_25(C_O1), .out_26(out_24), .out_27(out_28), .out_28(out_29),
    .out_29(out_30), .out_30(Y0_2), .in_2(or_3_out), .in_23(or_1_out), .in_18(trans_1_out_7));
  or or_1 (or_1_out, trans_2_out_6, demultiplexer_1_out9, trans_1_out_7);
  or or_2 (or_2_out, trans_1_out_8, trans_2_out_7);
  or or_3 (or_3_out, trans_2_out_7, demultiplexer_1_out8);
  mult mult_1 (
    .in_1(A0), .in_2(in_4), .in_3(in_3), .in_4(in_2), .in_5(B0), .in_6(in_14), .in_7(in_13), .in_8(in_12),
    .in_10(in_11), .in_11(in_11), .in_12(in_11), .in_9(in_11), .out_13(out_25), .out_14(out_26), .out_15(Y0));  // open: out_16, out_17, out_18, out_19
endmodule

module ALU_MAIN_CIRUIT (
  input  in_1,
  input  in_2,
  input  in_3,
  input  in_4,
  input  in_5,
  input  in_6,
  input  in_7,
  input  in_8,
  input  A0,
  input  in_10,
  input  in_11,
  input  in_12,
  input  in_13,
  input  in_14,
  input  in_15,
  input  in_16,
  input  in_17,
  input  in_18,
  input  in_19,
  input  in_20,
  input  in_21,
  output out_22,
  output out_23,
  output out_24,
  output out_25,
  output out_26,
  output out_27,
  output out_28,
  output out_29,
  output out_30,
  output out_31,
  output out_32,
  output out_33,
  output out_34,
  output out_35
);

  wire alu_assembly_1_neg;

  Hex_Digit_Display hex_digit_display_1 (.value({in_11, in_12, in_13, in_14}));  // open: dp
  Hex_Digit_Display hex_digit_display_2 (.value({in_6, in_7, in_8, A0}));  // open: dp
  ALU_Assembly alu_assembly_1 (
    .in_10(in_10), .in_16(in_16), .Arithmatic_EN(in_15), .out_32(out_32), .out_33(out_33), .out_34(out_34),
    .out_35(out_35), .in_2(in_6), .in_3(in_7), .in_4(in_8), .A0(A0), .in_6(in_2), .in_1(in_1), .in_7(in_3),
    .in_8(in_4), .in_9(in_5), .NEG(alu_assembly_1_neg), .C_O1(out_26), .out_24(out_27), .out_28(out_28),
    .out_29(out_29), .out_30(out_30), .Y0_2(out_31), .in_18(in_17), .in_19(in_18), .in_12(in_11),
    .in_13(in_12), .in_20(in_19), .in_14(in_13), .S0(in_20), .B0(in_14), .in_11(in_21), .out_25(out_22),
    .out_26(out_23), .Y0(out_24));
  Hex_Digit_Display hex_digit_display_3 (.value({out_32, out_33, out_34, out_35}));  // open: dp
  _7_Segment_Display u_7_segment_display_1 (.g(alu_assembly_1_neg));  // open: f, a, b, e, d, c, dp
  Hex_Digit_Display hex_digit_display_4 (.value({out_28, out_29, out_30, out_31}));  // open: dp
endmodule

module mult (
  input  in_1,
  input  in_2,
  input  in_3,
  input  in_4,
  input  in_5,
  input  in_6,
  input  in_7,
  input  in_8,
  input  in_9,
  input  in_10,
  input  in_11,
  input  in_12,
  output out_13,
  output out_14,
  output out_15,
  output out_16,
  output out_17,
  output out_18,
  output out_19
);

  wire and_1_out, and_2_out, and_3_out, and_4_out, and_5_out, and_6_out, and_7_out, and_8_out, and_9_out,
       and_10_out, and_11_out, and_12_out, and_13_out, and_14_out, and_15_out, n4_bit_adder_2_out_12,
       n4_bit_adder_2_out_13, n4_bit_adder_2_out_14, n4_bit_adder_3_out_12, n4_bit_adder_3_out_13,
       n4_bit_adder_3_out_14;

  and and_1 (and_1_out, in_8, in_4);
  and and_2 (and_2_out, in_8, in_3);
  and and_3 (and_3_out, in_8, in_2);
  and and_4 (and_4_out, in_8, in_1);
  and and_5 (and_5_out, in_7, in_4);
  and and_6 (and_6_out, in_7, in_3);
  _4_bit_Adder u_4_bit_adder_1 (
    .in_1(n4_bit_adder_2_out_12), .in_2(n4_bit_adder_2_out_13), .in_3(n4_bit_adder_2_out_14), .in_4(in_11),
    .in_5(and_4_out), .in_6(and_3_out), .in_7(and_2_out), .in_8(and_1_out), .in_9(in_12), .out_11(out_16),
    .out_12(out_15), .out_13(out_14), .out_14(out_13));  // open: out_10
  and and_7 (and_7_out, in_7, in_1);
  and and_8 (and_8_out, in_7, in_2);
  and and_9 (and_9_out, in_6, in_4);
  _4_bit_Adder u_4_bit_adder_2 (
    .in_1(n4_bit_adder_3_out_12), .in_2(n4_bit_adder_3_out_13), .in_3(n4_bit_adder_3_out_14), .in_4(in_10),
    .in_5(and_7_out), .in_6(and_8_out), .in_7(and_6_out), .in_8(and_5_out), .in_9(in_11), .out_11(out_17),
    .out_12(n4_bit_adder_2_out_12), .out_13(n4_bit_adder_2_out_13), .out_14(n4_bit_adder_2_out_14));  // open: out_10
  and and_10 (and_10_out, in_6, in_3);
  and and_11 (and_11_out, in_6, in_1);
  and and_12 (and_12_out, in_6, in_2);
  _4_bit_Adder u_4_bit_adder_3 (
    .in_1(and_15_out), .in_2(and_14_out), .in_3(and_13_out), .in_4(in_9), .in_5(and_11_out),
    .in_6(and_12_out), .in_7(and_10_out), .in_8(and_9_out), .in_9(in_10), .out_11(out_18),
    .out_12(n4_bit_adder_3_out_12), .out_13(n4_bit_adder_3_out_13), .out_14(n4_bit_adder_3_out_14));  // open: out_10
  and and_13 (and_13_out, in_5, in_4);
  and and_14 (and_14_out, in_5, in_3);
  and and_15 (and_15_out, in_5, in_2);
  and and_16 (out_19, in_5, in_1);
endmodule
